# Fritzing sketch Robocar (saved by Fritzing 0.9.3b)
breadboards: 1

parts:
  KY-1 = Keyes Relay [package=THT]
  IR1 = TSOP312.., 314.. [package=THT]
  Part1 = Arduino Uno (Rev3)
  KY-2 = Keyes Relay [package=THT]
  LED1 = LED - 5mm [color="Green (555nm)" package="5 mm [THT]"]
  R1 = Resistor [tolerance=±1% resistance=220 package=THT]
  M1 = DC Motor
  M2 = DC Motor
  M3 = DC Motor
  M4 = DC Motor
  BATT1 = 4xAA Switchable Battery Pack w/Bare Wire

nets:
  N1: KY-1.signal, Part1.D6_PWM
  N2: KY-1.power, IR1.Vs, Part1.VIN, KY-2.power
  GND: KY-1.ground, IR1.GND, Part1.GND, KY-2.ground, R1.Pin_0, M1.pin_2, M2.pin_2
  N3: KY-1.C, KY-2.C, BATT1.POS
  N4: KY-1.NO, M1.pin_1, M2.pin_1
  N5: IR1.Data, Part1.D2
  N6: Part1.D3_PWM, LED1.anode
  N7: Part1.D7, KY-2.signal
  N8: KY-2.NO, M3.pin_1, M4.pin_1
  N9: LED1.cathode, R1.Pin_1
  N10: M3.pin_2, M4.pin_2, BATT1.NEG

custom parts:
  Keyes Relay: The Keyes 5V relay module is suitable for SCM development, home appliance control. It uses a 5V~12V TIL control signal which can control DC / AC signal.
  4xAA Switchable Battery Pack w/Bare Wire: 4xAA Switchable Battery Pack with Bare Wire connection
